// Logisim project cpu.circ as structural Verilog
module registerFiles (
  input  [15:0] dataIn,
  input  [1:0] conIn,
  input  [1:0] conOut1,
  input  [1:0] conOut2,
  input  clock,
  output [15:0] outNum1,
  output [15:0] outNum2
);

  wire iswrite_1_out_2, iswrite_2_out_2, iswrite_3_out_2, iswrite_4_out_2;
  wire [15:0] demultiplexer_1_out0, demultiplexer_1_out1, demultiplexer_1_out2, demultiplexer_1_out3,
       register_1_q, register_2_q, register_3_q, register_4_q;

  Demultiplexer #(.select(2), .width(16)) demultiplexer_1 (
    .out0(demultiplexer_1_out0), .out1(demultiplexer_1_out1), .out2(demultiplexer_1_out2),
    .out3(demultiplexer_1_out3), .in(dataIn), .sel(conIn));  // open: en
  isWrite iswrite_1 (.\input (demultiplexer_1_out0), .out_2(iswrite_1_out_2));
  isWrite iswrite_2 (.\input (demultiplexer_1_out1), .out_2(iswrite_2_out_2));
  isWrite iswrite_3 (.\input (demultiplexer_1_out2), .out_2(iswrite_3_out_2));
  isWrite iswrite_4 (.\input (demultiplexer_1_out3), .out_2(iswrite_4_out_2));
  Register #(.width(16)) register_1 (
    .D(demultiplexer_1_out0), .en(iswrite_1_out_2), .Q(register_1_q), .clk(clock));  // open: clr
  Register #(.width(16)) register_2 (
    .D(demultiplexer_1_out1), .en(iswrite_2_out_2), .Q(register_2_q), .clk(clock));  // open: clr
  Register #(.width(16)) register_3 (
    .D(demultiplexer_1_out2), .en(iswrite_3_out_2), .Q(register_3_q), .clk(clock));  // open: clr
  Register #(.width(16)) register_4 (
    .D(demultiplexer_1_out3), .en(iswrite_4_out_2), .Q(register_4_q), .clk(clock));  // open: clr
  Multiplexer #(.select(2), .width(16)) multiplexer_1 (
    .in0(register_1_q), .in1(register_2_q), .in2(register_3_q), .in3(register_4_q), .out(outNum2),
    .sel(conOut2));  // open: en
  Multiplexer #(.select(2), .width(16)) multiplexer_2 (
    .in0(register_1_q), .in1(register_2_q), .in2(register_3_q), .in3(register_4_q), .out(outNum1),
    .sel(conOut1));  // open: en
endmodule

module main (
  input  in_1
);

  wire decode_1_p1, decode_1_p4, decode_1_p6, decode_1_p7, memRe, memWr, PC_p3, registerfiles_1_p1, undriven,
       undriven_2;
  wire [1:0] multiplexer_1_out, nPCsel;
  wire [2:0] decode_1_p2, decode_1_p3;
  wire [3:0] decode_1_p9;
  wire [7:0] decode_1_p5;
  wire [11:0] decode_1_p8;
  wire [15:0] alu_1_out_7, bit_extender_1_out, bit_extender_2_out, multiplexer_2_out, registerfiles_1_p3,
       registerfiles_1_p5, visitMe_p1;

  assign bit_extender_1_out = {{4{1'b0}}, decode_1_p8};  // Bit_Extender bit_extender_1
  assign bit_extender_2_out = {{8{1'b0}}, decode_1_p5};  // Bit_Extender bit_extender_2
  Multiplexer #(.width(2)) multiplexer_1 (.in0(2'b00), .out(multiplexer_1_out), .sel(in_1));  // open: in1, en
  Multiplexer #(.width(16)) multiplexer_2 (
    .in0(bit_extender_2_out), .in1(bit_extender_1_out), .out(multiplexer_2_out), .sel(undriven));  // open: en
  // PC PC: pin names not known; wires that end beside it: multiplexer_2_out, multiplexer_1_out, PC_p3
  // decode decode_1: pin names not known; wires that end beside it: decode_1_p1, decode_1_p2, decode_1_p3, decode_1_p4, decode_1_p5, decode_1_p6, decode_1_p7, decode_1_p8, decode_1_p9
  // memory visitMe: pin names not known; wires that end beside it: visitMe_p1, PC_p3, 1'b0, 1'b0, decode_1_p1
  controll controll_1 (.opcode(decode_1_p9), .funtc(decode_1_p2), .memWr(memWr), .memRe(memRe), .nPC_sel(nPCsel));
  Multiplexer #(.width(16)) multiplexer_3 (
    .in0({16{1'b1}}), .in1(alu_1_out_7), .out(visitMe_p1), .sel(undriven_2));  // open: en
  // registerFiles registerfiles_1: pin names not known; wires that end beside it: registerfiles_1_p1, decode_1_p7, registerfiles_1_p3, decode_1_p6, registerfiles_1_p5, decode_1_p9
  ALU alu_1 (
    .opcode(decode_1_p9), .rs(registerfiles_1_p3), .rt(registerfiles_1_p5), .imm(decode_1_p5),
    .party(decode_1_p3), .funtc(decode_1_p2), .out_7(alu_1_out_7));
endmodule

module ALU_R (
  input  [2:0] party,
  input  [2:0] funct,
  input  [15:0] rs,
  input  [15:0] rt,
  output [15:0] outPut
);

  wire comparator_1_lt;
  wire [15:0] adder_1_out, and_out, bit_extender_1_out, or_out, shifter_1_out, shifter_2_out, shifter_3_out,
       subtractor_1_out;

  Adder #(.width(16)) adder_1 (.a(rs), .b(rt), .out(adder_1_out));  // open: cin, cout
  Subtractor #(.width(16)) subtractor_1 (.a(rs), .b(rt), .out(subtractor_1_out));  // open: bin, bout
  Shifter #(.width(16)) shifter_1 (.in(rs), .\dist (rt[3:0]), .out(shifter_1_out));
  Shifter #(.width(16), .shift("lr")) shifter_2 (.in(rs), .\dist (rt[3:0]), .out(shifter_2_out));
  Shifter #(.width(16), .shift("ar")) shifter_3 (.in(rs), .\dist (rt[3:0]), .out(shifter_3_out));
  Comparator #(.width(16)) comparator_1 (.a(rs), .b(rt), .lt(comparator_1_lt));  // open: gt, eq
  assign or_out = rs | rt;  // OR_Gate or, 16 bits wide
  assign and_out = rs & rt;  // AND_Gate and, 16 bits wide
  assign bit_extender_1_out = {{15{1'b0}}, comparator_1_lt};  // Bit_Extender bit_extender_1
  Multiplexer #(.select(3), .width(16)) multiplexer_1 (
    .in0(or_out), .in1(and_out), .in2(adder_1_out), .in3(subtractor_1_out), .in4(shifter_1_out),
    .in5(shifter_2_out), .in6(shifter_3_out), .in7(bit_extender_1_out), .out(outPut), .sel(funct));  // open: en
endmodule

module memory (
  input  [15:0] DataIn,
  input  [15:0] Address,
  input  Clear,
  input  MemWrite,
  input  clock,
  output [15:0] DataOut
);

  wire not_1_out;

  RAM #(.addrWidth(16), .dataWidth(16)) ram_1 (
    .addr(Address), .data(DataOut), .sel(1'b1), .clk(clock), .ld(not_1_out), .clr(Clear));
  not not_1 (not_1_out, MemWrite);
  assign DataOut = MemWrite ? DataIn : 16'bz;  // Controlled_Buffer controlled_buffer_1
endmodule

module ALU (
  input  [7:0] imm,
  input  [3:0] opcode,
  input  [15:0] rs,
  input  [15:0] rt,
  input  [2:0] party,
  input  [2:0] funtc,
  output [15:0] out_7
);

  wire comparator_1_eq, not_1_out;
  wire [15:0] adder_1_out, adder_2_out, andi_out, bit_extender_1_out, bit_extender_2_out, bit_extender_3_out,
       bit_extender_4_out, ori_out, R_output, shifter_1_out;

  assign bit_extender_1_out = {{8{1'b0}}, imm};  // Bit_Extender bit_extender_1
  assign bit_extender_2_out = {{8{imm[7]}}, imm};  // Bit_Extender bit_extender_2
  ALU_R R (.party(party), .rs(rs), .rt(rt), .funct(funtc), .outPut(R_output));
  Shifter #(.width(16)) shifter_1 (.in(bit_extender_1_out), .\dist (4'b1000), .out(shifter_1_out));
  assign ori_out = rs | bit_extender_1_out;  // OR_Gate ori, 16 bits wide
  Adder #(.width(16)) adder_1 (.a(rs), .b(bit_extender_2_out), .out(adder_1_out));  // open: cin, cout
  assign andi_out = rs & bit_extender_1_out;  // AND_Gate andi, 16 bits wide
  Adder #(.width(16)) adder_2 (.a(bit_extender_2_out), .b(rs), .out(adder_2_out));  // open: cin, cout
  Comparator #(.width(16)) comparator_1 (.a(rs), .b(rt), .eq(comparator_1_eq));  // open: gt, lt
  assign bit_extender_3_out = {{15{1'b0}}, comparator_1_eq};  // Bit_Extender bit_extender_3
  assign bit_extender_4_out = {{15{1'b0}}, not_1_out};  // Bit_Extender bit_extender_4
  not not_1 (not_1_out, comparator_1_eq);
  Multiplexer #(.select(4), .width(16)) multiplexer_1 (
    .in0(R_output), .in2(shifter_1_out), .in3(ori_out), .in4(adder_1_out), .in5(andi_out), .in6(adder_2_out),
    .in7(adder_2_out), .in9(bit_extender_3_out), .in10(bit_extender_4_out), .out(out_7), .sel(opcode));  // open: in1, in8, in11, in12, in13, in14, in15, en

  // Notes on the sheet:
  //   lui
  //   addi
endmodule

module isWrite (
  input  [15:0] \input ,
  output out_2
);

  or or_1 (out_2, \input [0], \input [1], \input [2], \input [3], \input [4], \input [5], \input [6], \input [7], \input [9], \input [10], \input [11], \input [12], \input [13], \input [14], \input [15], \input [8]);
endmodule

// pc
module PC (
  input  reset,
  input  [15:0] offset,
  input  [1:0] control,
  output [15:0] addr
);

  wire clock_1_out;
  wire [15:0] adder_1_out, adder_2_out, and_1_out, or_1_out, register_1_q;

  Register #(.width(16)) register_1 (.D(addr), .en(1'b1), .Q(register_1_q), .clk(clock_1_out), .clr(reset));
  Clock clock_1 (.out(clock_1_out));
  assign and_1_out = register_1_q & 16'hf000;  // AND_Gate and_1, 16 bits wide
  Adder #(.width(16)) adder_1 (.a(register_1_q), .b(16'h1), .out(adder_1_out));  // open: cin, cout
  assign or_1_out = and_1_out | offset;  // OR_Gate or_1, 16 bits wide
  Adder #(.width(16)) adder_2 (.a(adder_1_out), .b(offset), .out(adder_2_out));  // open: cin, cout
  Multiplexer #(.select(2), .width(16)) multiplexer_1 (
    .in0(adder_1_out), .in1(adder_2_out), .in2(or_1_out), .in3({16{1'b0}}), .out(addr), .sel(control));  // open: en
endmodule

module decode (
  input  [15:0] \input ,
  output [3:0] opcode,
  output [2:0] funtc,
  output [2:0] party,
  output [1:0] rd,
  output [7:0] offset,
  output [1:0] rt,
  output [1:0] rs,
  output [11:0] imm
);


  assign funtc = \input [2:0];
  assign imm = \input [11:0];
  assign offset = \input [7:0];
  assign opcode = \input [15:12];
  assign party = \input [5:3];
  assign rd = \input [7:6];
  assign rs = \input [11:10];
  assign rt = \input [9:8];
endmodule

module main_2 (
);

  wire clock, controll_1_memre, mem_clear, mem_wr, pc_reset;
  wire [1:0] rd, re_con1, re_con2, re_incon;
  wire [2:0] decode_1_funtc, party;
  wire [3:0] decode_1_opcode;
  wire [7:0] offset;
  wire [11:0] imm;
  wire [15:0] alu_1_out_7, mem_addr, mem_in, mem_out, pc_ofect, re_in, re_num1;

  memory memory_1 (
    .DataIn(mem_in), .Address(mem_addr), .Clear(mem_clear), .MemWrite(mem_wr), .clock(clock),
    .DataOut(mem_out));
  PC pc_1 (.addr(mem_addr), .reset(pc_reset), .offset(pc_ofect), .control(2'b00));
  registerFiles registerfiles_1 (
    .clock(clock), .conIn(re_incon), .dataIn(re_in), .conOut1(re_con1), .outNum1(re_num1), .conOut2(re_con2),
    .outNum2(re_num1));
  Clock clock_1 (.out(clock));
  decode decode_1 (
    .\input (mem_out), .opcode(decode_1_opcode), .funtc(decode_1_funtc), .party(party), .rd(rd),
    .offset(offset), .rt(re_con2), .rs(re_con1), .imm(imm));
  controll controll_1 (
    .opcode(decode_1_opcode), .funtc(decode_1_funtc), .memWr(mem_wr), .memRe(controll_1_memre));  // open: nPC_sel
  // Probe on offset
  ALU alu_1 (
    .opcode(decode_1_opcode), .rs(re_num1), .rt(re_num1), .imm(offset), .funtc(decode_1_funtc),
    .out_7(alu_1_out_7));  // open: party
  // also tied to GND on the sheet: mem_wr

  // Other names for the same wires on the sheet: pc_addr[15:0] = mem_addr; re_num2[15:0] = re_num1
endmodule

module controll (
  input  [3:0] opcode,
  input  [2:0] funtc,
  output memWr,
  output memRe,
  output [1:0] nPC_sel
);

  wire comparator_3_eq, comparator_4_eq, comparator_5_eq, or_1_out;
  wire [1:0] bit_extender_1_out;

  Comparator #(.width(4)) comparator_1 (.a(opcode), .b(4'b0111), .eq(memWr));  // open: gt, lt
  Comparator #(.width(4)) comparator_2 (.a(opcode), .b(4'b0110), .eq(memRe));  // open: gt, lt
  Comparator #(.width(4)) comparator_3 (.a(opcode), .b(4'b1000), .eq(comparator_3_eq));  // open: gt, lt
  Comparator #(.width(4)) comparator_4 (.a(opcode), .b(4'b1001), .eq(comparator_4_eq));  // open: gt, lt
  Comparator #(.width(4)) comparator_5 (.a(opcode), .b(4'b1010), .eq(comparator_5_eq));  // open: gt, lt
  Comparator #(.width(4)) comparator_6 (.a(opcode), .b(4'b0001));  // open: gt, eq, lt
  Comparator #(.width(4)) comparator_7 (.a(opcode), .b(4'b0010));  // open: gt, eq, lt
  Comparator #(.width(4)) comparator_8 (.a(opcode), .b(4'b0011));  // open: gt, eq, lt
  Comparator #(.width(4)) comparator_9 (.a(opcode), .b(4'b0100));  // open: gt, eq, lt
  Comparator #(.width(4)) comparator_10 (.a(opcode), .b(4'b0101));  // open: gt, eq, lt
  Comparator #(.width(4)) comparator_11 (.a(opcode), .b(4'b0000));  // open: gt, eq, lt
  Comparator #(.width(3)) comparator_12 (.a(funtc), .b(3'b000));  // open: gt, eq, lt
  Comparator #(.width(3)) comparator_13 (.a(funtc), .b(3'b001));  // open: gt, eq, lt
  Comparator #(.width(3)) comparator_14 (.a(funtc), .b(3'b010));  // open: gt, eq, lt
  Comparator #(.width(3)) comparator_15 (.a(funtc), .b(3'b011));  // open: gt, eq, lt
  Comparator #(.width(3)) comparator_16 (.a(funtc), .b(3'b100));  // open: gt, eq, lt
  or or_1 (or_1_out, comparator_4_eq, comparator_5_eq);
  assign bit_extender_1_out = {{1{1'b0}}, or_1_out};  // Bit_Extender bit_extender_1
  Multiplexer #(.width(2)) multiplexer_1 (
    .in0(bit_extender_1_out), .in1(2'b10), .out(nPC_sel), .sel(comparator_3_eq));  // open: en
endmodule
